// Logisim project IICSE_076_ASS07_a.circ as structural Verilog: 1 circuit, main circuit main
module main (
  input  [7:0] X,
  output [7:0] _2X
);

  Adder adder_1 (.a(X), .b(X), .out(_2X));  // open: cin, cout
endmodule
