// Logisim project IICSE_076_ASS07_b.circ as structural Verilog: 1 circuit, main circuit main
module main (
  input  [7:0] x,
  input  [7:0] y,
  output [7:0] _2x__y
);

  wire [7:0] adder_1_out;

  Adder adder_1 (.a(x), .b(x), .out(adder_1_out));  // open: cin, cout
  Adder adder_2 (.a(adder_1_out), .b(y), .out(_2x__y));  // open: cin, cout
endmodule
