// Logisim project IICSE_076_ASS07_c.circ as structural Verilog: 1 circuit, main circuit main
module main (
  input  [7:0] x,
  input  [7:0] y,
  output [7:0] average_of_x_y
);

  wire [7:0] adder_1_out;

  Adder adder_1 (.a(x), .b(y), .out(adder_1_out));  // open: cin, cout
  Divider divider_1 (.a(adder_1_out), .b(8'h2), .out(average_of_x_y));  // open: upper, rem
endmodule
