// Logisim project IICSE_076_ASS07_d.circ as structural Verilog: 1 circuit, main circuit main
module main (
  input  [7:0] x,
  output [7:0] x_2
);

  Multiplier multiplier_1 (.a(x), .b(x), .out(x_2));  // open: cin, cout
endmodule
