// Logisim project IICSE_076_ASS07_e.circ as structural Verilog: 1 circuit, main circuit main
module main (
  input  [7:0] x,
  input  [7:0] y,
  output [7:0] x_y
);

  Multiplier multiplier_1 (.a(x), .b(y), .out(x_y));  // open: cin, cout
endmodule
