// Logisim project IICSE_076_ASS07_f.circ as structural Verilog: 1 circuit, main circuit main
module main (
  input  [7:0] x,
  output [7:0] x_prime
);

  Negator negator_1 (.in(x), .out(x_prime));
endmodule
