// Logisim project IICSE_076_ASS07_g.circ as structural Verilog: 1 circuit, main circuit main
module main (
  input  [7:0] x,
  output [7:0] x_6
);

  wire [7:0] multiplier_1_out, multiplier_2_out;

  Multiplier multiplier_1 (.a(x), .b(x), .out(multiplier_1_out));  // open: cin, cout
  Multiplier multiplier_2 (.a(multiplier_1_out), .b(multiplier_1_out), .out(multiplier_2_out));  // open: cin, cout
  Multiplier multiplier_3 (.a(multiplier_2_out), .b(multiplier_1_out), .out(x_6));  // open: cin, cout
endmodule
