// Logisim project u19cs076.circ as structural Verilog: 1 circuit, main circuit main
module main (
  input  [15:0] x,
  output [7:0] input_x,
  output [3:0] LSB,
  output [7:0] input_y,
  output [3:0] MSB,
  output [7:0] FINAL_OUTPUT
);

  wire [7:0] multiplier_1_out;

  assign input_x = {{4{1'b0}}, x[3:0]};  // Bit_Extender bit_extender_1
  Multiplier multiplier_1 (.a(input_x), .b(x[11:4]), .out(multiplier_1_out));  // open: cin, cout
  Multiplier multiplier_2 (.a(multiplier_1_out), .b(multiplier_1_out), .out(FINAL_OUTPUT));  // open: cin, cout

  assign input_y = x[11:4];
  assign LSB = x[3:0];
  assign MSB = x[15:12];

  // Notes on the sheet:
  //   U19CS076 ASSESSMENT
endmodule
