// Logisim project IICSE_076_Ass08_01.circ as structural Verilog: 2 circuits, main circuit AX+Y
// ax
module subckt (
  input  [7:0] X,
  input  [7:0] Y,
  output [7:0] XY
);

  Multiplier multiplier_1 (.a(X), .b(Y), .out(XY));  // open: cin, cout
endmodule

module AX_Y (
  input  [7:0] A,
  input  [7:0] X,
  input  [7:0] Y,
  output [7:0] AX_Y
);

  wire [7:0] ASSGN7_E__xy;

  subckt ASSGN7_E_ (.X(A), .Y(X), .XY(ASSGN7_E__xy));
  Adder adder_1 (.a(ASSGN7_E__xy), .b(Y), .out(AX_Y));  // open: cin, cout
endmodule
