// Logisim project IICSE_076_Ass08_02.circ as structural Verilog: 2 circuits, main circuit Average of 4 num
// AVG
module Sub_ckt_assgn7_C (
  input  [7:0] X,
  input  [7:0] Y,
  output [7:0] out_3
);

  wire [7:0] adder_1_out;

  Adder adder_1 (.a(X), .b(Y), .out(adder_1_out));  // open: cin, cout
  Divider divider_1 (.a(adder_1_out), .b(8'h2), .out(out_3));  // open: upper, rem
endmodule

module Average_of_4_num (
  input  [7:0] A,
  input  [7:0] B,
  input  [7:0] C,
  input  [7:0] D,
  output [7:0] out_5
);

  wire [7:0] ASSGN7_C__2_out_3, ASSGN7_C__out_3;

  Sub_ckt_assgn7_C ASSGN7_C_ (.X(A), .Y(B), .out_3(ASSGN7_C__out_3));
  Sub_ckt_assgn7_C ASSGN7_C__2 (.X(C), .Y(D), .out_3(ASSGN7_C__2_out_3));
  Sub_ckt_assgn7_C ASSGN7_C__3 (.X(ASSGN7_C__out_3), .Y(ASSGN7_C__2_out_3), .out_3(out_5));
endmodule
