// Logisim project IICSE_076_Ass08_03.circ as structural Verilog: 2 circuits, main circuit X^2+2XY+Y^2
// (x+y)^2
module assgn7_d (
  input  [7:0] X,
  output [7:0] X_2
);

  Multiplier multiplier_1 (.a(X), .b(X), .out(X_2));  // open: cin, cout
endmodule

module X_2_2XY_Y_2 (
  input  [7:0] X,
  input  [7:0] Y,
  output [7:0] X_Y__2_X_2_2XY_Y_2
);

  wire [7:0] adder_1_out;

  Adder adder_1 (.a(X), .b(Y), .out(adder_1_out));  // open: cin, cout
  assgn7_d ASSGN7_D_ (.X(adder_1_out), .X_2(X_Y__2_X_2_2XY_Y_2));
endmodule
