// Logisim project IICSE_076_Ass08_04.circ as structural Verilog: 3 circuits, main circuit 4X'
// x'
module X (
  input  [7:0] X,
  output [7:0] X_prime
);

  Negator negator_1 (.in(X), .out(X_prime));
endmodule

// 4X
module XY (
  input  [7:0] X,
  input  [7:0] y,
  output [7:0] _2X
);

  Multiplier multiplier_1 (.a(X), .b(y), .out(_2X));  // open: cin, cout
endmodule

module _4X (
  input  [7:0] in_1,
  output [7:0] _4x_prime
);

  wire [7:0] ASSGN7_F__x_prime;

  X ASSGN7_F_ (.X(in_1), .X_prime(ASSGN7_F__x_prime));
  XY ASSGN7_E_ (.X(ASSGN7_F__x_prime), .y(8'h4), ._2X(_4x_prime));
endmodule
