// Logisim project IICSE_076_Ass08_05.circ as structural Verilog: 3 circuits, main circuit A*X^6
// X^6
module main (
  input  [7:0] X,
  output [7:0] X_6
);

  wire [7:0] multiplier_1_out, multiplier_2_out;

  Multiplier multiplier_1 (.a(X), .b(X), .out(multiplier_1_out), .cin({8{1'b0}}));  // open: cout
  Multiplier multiplier_2 (
    .a(multiplier_1_out), .b(multiplier_1_out), .out(multiplier_2_out), .cin({8{1'b0}}));  // open: cout
  Multiplier multiplier_3 (.a(multiplier_2_out), .b(multiplier_1_out), .out(X_6), .cin({8{1'b0}}));  // open: cout
endmodule

// ax^6
module XY (
  input  [7:0] X,
  input  [7:0] Y,
  output [7:0] XY
);

  Multiplier multiplier_1 (.a(X), .b(Y), .out(XY), .cin({8{1'b0}}));  // open: cout
endmodule

module A_X_6 (
  input  [7:0] A,
  input  [7:0] X,
  output [7:0] A_X_6
);

  wire [7:0] ASSGN7_G_x_6;

  main ASSGN7_G (.X(X), .X_6(ASSGN7_G_x_6));
  XY ASSGN7_E_ (.X(A), .Y(ASSGN7_G_x_6), .XY(A_X_6));
endmodule
