// Logisim project IICSE_076_ASS02_02.circ as structural Verilog: 1 circuit, main circuit main
module main (
  input  A1,
  input  A3,
  input  B1,
  input  B3,
  input  C,
  input  A2,
  input  A4,
  input  B2,
  input  in_9,
  output O1,
  output o3,
  output O2,
  output O4,
  output carry_out
);

  wire and_1_out, and_2_out, and_3_out, and_4_out, and_5_out, and_6_out, and_7_out, and_8_out, or_1_out,
       or_2_out, or_3_out, xor_1_out, xor_2_out, xor_5_out, xor_6_out;

  xor xor_1 (xor_1_out, A1, B1);
  and and_1 (and_1_out, B1, A1);
  xor xor_2 (xor_2_out, A2, B2);
  and and_2 (and_2_out, B2, A2);
  xor xor_3 (O1, xor_1_out, C);
  xor xor_4 (O2, xor_2_out, or_1_out);
  and and_3 (and_3_out, or_1_out, xor_2_out);
  and and_4 (and_4_out, C, xor_1_out);
  or or_1 (or_1_out, and_4_out, and_1_out);
  or or_2 (or_2_out, and_3_out, and_2_out);
  xor xor_5 (xor_5_out, A3, B3);
  and and_5 (and_5_out, B3, A3);
  xor xor_6 (xor_6_out, A4, in_9);
  and and_6 (and_6_out, in_9, A4);
  xor xor_7 (o3, xor_5_out, or_2_out);
  and and_7 (and_7_out, or_2_out, xor_5_out);
  xor xor_8 (O4, xor_6_out, or_3_out);
  and and_8 (and_8_out, or_3_out, xor_6_out);
  or or_3 (or_3_out, and_7_out, and_5_out);
  or or_4 (carry_out, and_8_out, and_6_out);

  // Notes on the sheet:
  //   4 bit full adder
endmodule
