// Logisim project IICSE_076_ASS02_03.circ as structural Verilog: 1 circuit, main circuit main
module main (
  input  A0,
  input  A2,
  input  B0,
  input  B2,
  input  A1,
  input  A3,
  input  B3,
  input  B1,
  output D0,
  output D2,
  output D1,
  output D3,
  output Bout
);

  wire and_1_out, and_2_out, and_3_out, and_4_out, and_5_out, and_6_out, and_7_out, and_8_out, and_9_out,
       and_10_out, not_1_out, not_2_out, not_3_out, not_4_out, or_1_out, or_2_out, xor_2_out, xor_4_out,
       xor_5_out;

  not not_1 (not_1_out, A0);
  not not_2 (not_2_out, A1);
  and and_1 (and_1_out, not_2_out, B1);
  and and_2 (and_2_out, B1, and_4_out);
  and and_3 (and_3_out, not_2_out, and_4_out);
  xor xor_1 (D0, A0, B0);
  and and_4 (and_4_out, not_1_out, B0);
  xor xor_2 (xor_2_out, A1, B1);
  xor xor_3 (D1, xor_2_out, and_4_out);
  or or_1 (or_1_out, and_1_out, and_2_out, and_3_out);
  not not_3 (not_3_out, A2);
  not not_4 (not_4_out, A3);
  and and_5 (and_5_out, not_3_out, B2);
  and and_6 (and_6_out, B2, or_1_out);
  and and_7 (and_7_out, not_3_out, or_1_out);
  xor xor_4 (xor_4_out, A3, B3);
  and and_8 (and_8_out, not_4_out, B3);
  and and_9 (and_9_out, B3, or_2_out);
  and and_10 (and_10_out, not_4_out, or_2_out);
  xor xor_5 (xor_5_out, A2, B2);
  xor xor_6 (D2, xor_5_out, or_1_out);
  or or_2 (or_2_out, and_5_out, and_6_out, and_7_out);
  xor xor_7 (D3, xor_4_out, or_2_out);
  or or_3 (Bout, and_8_out, and_9_out, and_10_out);

  // Notes on the sheet:
  //   4 bit half subtractor
endmodule
