// Logisim project IICSE_076_ASS02_05.circ as structural Verilog: 1 circuit, main circuit main
module main (
  input  A4,
  input  B4,
  input  A0,
  input  A2,
  input  B4_2,
  input  B6,
  input  B0,
  input  B2,
  input  A5,
  input  A7,
  input  A1,
  input  A3,
  input  B5,
  input  B7,
  input  B1,
  input  B3,
  output S0,
  output S4,
  output S6,
  output S2,
  output S5,
  output S7,
  output S1,
  output S3,
  output Cout
);

  wire and_1_out, and_2_out, and_3_out, and_4_out, and_5_out, and_6_out, and_7_out, and_8_out, and_9_out,
       and_10_out, and_11_out, and_12_out, and_13_out, and_14_out, and_15_out, and_16_out, and_17_out,
       and_18_out, and_19_out, and_20_out, and_21_out, and_22_out, or_1_out, or_2_out, or_3_out, or_4_out,
       or_5_out, or_6_out, xor_2_out, xor_4_out, xor_5_out, xor_8_out, xor_9_out, xor_12_out, xor_13_out;

  and and_1 (and_1_out, A1, B1);
  and and_2 (and_2_out, B1, and_4_out);
  and and_3 (and_3_out, A1, and_4_out);
  xor xor_1 (S0, A0, B0);
  and and_4 (and_4_out, A0, B0);
  xor xor_2 (xor_2_out, A1, B1);
  xor xor_3 (S1, xor_2_out, and_4_out);
  or or_1 (or_1_out, and_1_out, and_2_out, and_3_out);
  xor xor_4 (xor_4_out, A2, B2);
  and and_5 (and_5_out, A2, B2);
  and and_6 (and_6_out, B2, or_1_out);
  and and_7 (and_7_out, A2, or_1_out);
  xor xor_5 (xor_5_out, A3, B3);
  and and_8 (and_8_out, A3, B3);
  and and_9 (and_9_out, B3, or_2_out);
  and and_10 (and_10_out, A3, or_2_out);
  xor xor_6 (S3, xor_5_out, or_2_out);
  xor xor_7 (S2, xor_4_out, or_1_out);
  or or_2 (or_2_out, and_5_out, and_6_out, and_7_out);
  or or_3 (or_3_out, and_8_out, and_9_out, and_10_out);
  and and_11 (and_11_out, A5, B5);
  and and_12 (and_12_out, B5, or_4_out);
  and and_13 (and_13_out, A5, or_4_out);
  ExactlyOne xor_8 (.out(xor_8_out), .in0(A4), .in1(A4), .in4(B4_2));
  and and_14 (and_14_out, A4, B4_2);
  and and_15 (and_15_out, B4_2, or_3_out);
  and and_16 (and_16_out, A4, or_3_out);
  xor xor_9 (xor_9_out, A5, B5);
  xor xor_10 (S4, xor_8_out, or_3_out);
  or or_4 (or_4_out, and_14_out, and_15_out, and_16_out);
  xor xor_11 (S5, xor_9_out, or_4_out);
  or or_5 (or_5_out, and_11_out, and_12_out, and_13_out);
  xor xor_12 (xor_12_out, B4, B6);
  and and_17 (and_17_out, B4, B6);
  and and_18 (and_18_out, B6, or_5_out);
  and and_19 (and_19_out, B4, or_5_out);
  xor xor_13 (xor_13_out, A7, B7);
  and and_20 (and_20_out, A7, B7);
  and and_21 (and_21_out, B7, or_6_out);
  and and_22 (and_22_out, A7, or_6_out);
  xor xor_14 (S7, xor_13_out, or_6_out);
  xor xor_15 (S6, xor_12_out, or_5_out);
  or or_6 (or_6_out, and_17_out, and_18_out, and_19_out);
  or or_7 (Cout, and_20_out, and_21_out, and_22_out);

  // Notes on the sheet:
  //   8 bit half adder
endmodule
