// Logisim project IICSE_076_ASS02_07.circ as structural Verilog: 1 circuit, main circuit main
module main (
  input  A1,
  input  A3,
  input  B1,
  input  B3,
  input  C,
  input  A2,
  input  A4,
  input  B2,
  input  in_9,
  input  A5,
  input  A6,
  input  B1_2,
  input  B6,
  input  A7,
  input  A8,
  input  B7,
  input  in_17,
  output O1,
  output o3,
  output O2,
  output O4,
  output O5,
  output O6,
  output O7,
  output O8,
  output carry_out
);

  wire and_1_out, and_2_out, and_3_out, and_4_out, and_5_out, and_6_out, and_7_out, and_8_out, and_9_out,
       and_10_out, and_11_out, and_12_out, and_13_out, and_14_out, and_15_out, and_16_out, or_1_out,
       or_2_out, or_3_out, or_4_out, or_5_out, or_6_out, or_7_out, xor_1_out, xor_2_out, xor_3_out,
       xor_4_out, xor_9_out, xor_10_out, xor_11_out, xor_12_out;

  xor xor_1 (xor_1_out, A1, B1);
  and and_1 (and_1_out, B1, A1);
  xor xor_2 (xor_2_out, A2, B2);
  and and_2 (and_2_out, B2, A2);
  xor xor_3 (xor_3_out, A5, B1_2);
  and and_3 (and_3_out, B1_2, A5);
  xor xor_4 (xor_4_out, A7, B7);
  and and_4 (and_4_out, B7, A7);
  xor xor_5 (O1, xor_1_out, C);
  xor xor_6 (O2, xor_2_out, or_3_out);
  and and_5 (and_5_out, or_3_out, xor_2_out);
  xor xor_7 (O5, xor_3_out, or_6_out);
  and and_6 (and_6_out, or_6_out, xor_3_out);
  xor xor_8 (O7, xor_4_out, or_1_out);
  and and_7 (and_7_out, or_1_out, xor_4_out);
  and and_8 (and_8_out, C, xor_1_out);
  or or_1 (or_1_out, and_6_out, and_3_out);
  or or_2 (or_2_out, and_7_out, and_4_out);
  or or_3 (or_3_out, and_8_out, and_1_out);
  or or_4 (or_4_out, and_5_out, and_2_out);
  and and_9 (and_9_out, B6, A6);
  xor xor_9 (xor_9_out, A3, B3);
  and and_10 (and_10_out, B3, A3);
  xor xor_10 (xor_10_out, A4, in_9);
  and and_11 (and_11_out, in_9, A4);
  xor xor_11 (xor_11_out, A6, B6);
  xor xor_12 (xor_12_out, A8, in_17);
  and and_12 (and_12_out, in_17, A8);
  xor xor_13 (o3, xor_9_out, or_4_out);
  and and_13 (and_13_out, or_4_out, xor_9_out);
  xor xor_14 (O4, xor_10_out, or_5_out);
  and and_14 (and_14_out, or_5_out, xor_10_out);
  xor xor_15 (O6, xor_11_out, or_2_out);
  and and_15 (and_15_out, or_2_out, xor_11_out);
  xor xor_16 (O8, xor_12_out, or_7_out);
  and and_16 (and_16_out, or_7_out, xor_12_out);
  or or_5 (or_5_out, and_13_out, and_10_out);
  or or_6 (or_6_out, and_14_out, and_11_out);
  or or_7 (or_7_out, and_15_out, and_9_out);
  or or_8 (carry_out, and_16_out, and_12_out);

  // Notes on the sheet:
  //   8 bit full adder
endmodule
