// Logisim project IICSE_076_ASS02_08.circ as structural Verilog: 1 circuit, main circuit main
module main (
  input  A0,
  input  A2,
  input  A4,
  input  A6,
  input  B0,
  input  B2,
  input  B4,
  input  B6,
  input  Bin,
  input  A1,
  input  A3,
  input  A5,
  input  A7,
  input  B1,
  input  B3,
  input  B5,
  input  B7,
  output D0,
  output D2,
  output D4,
  output D6,
  output D1,
  output D3,
  output D5,
  output D7,
  output Bout
);

  wire and_1_out, and_2_out, and_3_out, and_4_out, and_5_out, and_6_out, and_7_out, and_8_out, and_9_out,
       and_10_out, and_11_out, and_12_out, and_13_out, and_14_out, and_15_out, and_16_out, and_17_out,
       and_18_out, and_19_out, and_20_out, and_21_out, and_22_out, and_23_out, and_24_out, not_1_out,
       not_2_out, not_3_out, not_4_out, not_5_out, not_6_out, not_7_out, not_8_out, or_1_out, or_2_out,
       or_3_out, or_4_out, or_5_out, or_6_out, or_7_out, xor_1_out, xor_2_out, xor_5_out, xor_6_out,
       xor_9_out, xor_10_out, xor_13_out, xor_14_out;

  not not_1 (not_1_out, A0);
  not not_2 (not_2_out, A1);
  and and_1 (and_1_out, not_2_out, B1);
  and and_2 (and_2_out, B1, or_1_out);
  and and_3 (and_3_out, not_2_out, or_1_out);
  xor xor_1 (xor_1_out, A0, B0);
  and and_4 (and_4_out, not_1_out, B0);
  and and_5 (and_5_out, B0, Bin);
  and and_6 (and_6_out, not_1_out, Bin);
  xor xor_2 (xor_2_out, A1, B1);
  xor xor_3 (D0, xor_1_out, Bin);
  or or_1 (or_1_out, and_4_out, and_5_out, and_6_out);
  xor xor_4 (D1, xor_2_out, or_1_out);
  or or_2 (or_2_out, and_1_out, and_2_out, and_3_out);
  not not_3 (not_3_out, A2);
  not not_4 (not_4_out, A3);
  xor xor_5 (xor_5_out, A2, B2);
  and and_7 (and_7_out, not_3_out, B2);
  and and_8 (and_8_out, B2, or_2_out);
  and and_9 (and_9_out, not_3_out, or_2_out);
  xor xor_6 (xor_6_out, A3, B3);
  and and_10 (and_10_out, not_4_out, B3);
  and and_11 (and_11_out, B3, or_3_out);
  and and_12 (and_12_out, not_4_out, or_3_out);
  xor xor_7 (D3, xor_6_out, or_3_out);
  xor xor_8 (D2, xor_5_out, or_2_out);
  or or_3 (or_3_out, and_7_out, and_8_out, and_9_out);
  or or_4 (or_4_out, and_10_out, and_11_out, and_12_out);
  not not_5 (not_5_out, A4);
  not not_6 (not_6_out, A5);
  xor xor_9 (xor_9_out, A4, B4);
  and and_13 (and_13_out, not_5_out, B4);
  and and_14 (and_14_out, B4, or_4_out);
  and and_15 (and_15_out, not_5_out, or_4_out);
  xor xor_10 (xor_10_out, A5, B5);
  and and_16 (and_16_out, not_6_out, B5);
  and and_17 (and_17_out, B5, or_5_out);
  and and_18 (and_18_out, not_6_out, or_5_out);
  xor xor_11 (D5, xor_10_out, or_5_out);
  xor xor_12 (D4, xor_9_out, or_4_out);
  or or_5 (or_5_out, and_13_out, and_14_out, and_15_out);
  or or_6 (or_6_out, and_16_out, and_17_out, and_18_out);
  not not_7 (not_7_out, A6);
  not not_8 (not_8_out, A7);
  xor xor_13 (xor_13_out, A6, B6);
  and and_19 (and_19_out, not_7_out, B6);
  and and_20 (and_20_out, B6, or_6_out);
  and and_21 (and_21_out, not_7_out, or_6_out);
  xor xor_14 (xor_14_out, A7, B7);
  and and_22 (and_22_out, not_8_out, B7);
  and and_23 (and_23_out, B7, or_7_out);
  and and_24 (and_24_out, not_8_out, or_7_out);
  xor xor_15 (D6, xor_13_out, or_6_out);
  or or_7 (or_7_out, and_19_out, and_20_out, and_21_out);
  xor xor_16 (D7, xor_14_out, or_7_out);
  or or_8 (Bout, and_22_out, and_23_out, and_24_out);

  // Notes on the sheet:
  //   8 bit full subtractor
endmodule
