// Logisim project IICSE_076_Ass01_01.circ as structural Verilog: 1 circuit, main circuit main
module main (
  input  x1,
  input  x0,
  output S,
  output C
);

  wire and_1_out, and_2_out, not_1_out, not_2_out;

  not not_1 (not_1_out, x0);
  not not_2 (not_2_out, x1);
  and and_1 (and_1_out, not_1_out, x1);
  and and_2 (and_2_out, x0, not_2_out);
  and and_3 (C, x1, x0);
  or or_1 (S, and_1_out, and_2_out);
endmodule
