// Logisim project IICSE_076_Ass01_03.circ as structural Verilog: 1 circuit, main circuit main
// Sum
module main (
  input  Cin,
  input  B,
  input  A,
  output ADD,
  output CarryOut
);

  wire and_1_out, and_2_out, and_3_out, and_4_out, and_5_out, and_6_out, and_7_out, not_1_out, not_2_out,
       not_3_out, not_4_out, not_5_out, not_6_out;

  not not_1 (not_1_out, B);
  not not_2 (not_2_out, A);
  not not_3 (not_3_out, Cin);
  not not_4 (not_4_out, A);
  not not_5 (not_5_out, Cin);
  not not_6 (not_6_out, B);
  and and_1 (and_1_out, not_1_out, not_2_out, Cin);
  and and_2 (and_2_out, not_3_out, not_4_out, B);
  and and_3 (and_3_out, not_5_out, A, not_6_out);
  and and_4 (and_4_out, A, B, Cin);
  and and_5 (and_5_out, B, Cin);
  and and_6 (and_6_out, A, Cin);
  and and_7 (and_7_out, B, A);
  or or_1 (ADD, and_1_out, and_2_out, and_3_out, and_4_out);
  or or_2 (CarryOut, and_5_out, and_6_out, and_7_out);
endmodule
