// Logisim project IICSE_076_ASS02_01.circ as structural Verilog: 1 circuit, main circuit main
module main (
  input  A1,
  input  A3,
  input  B,
  input  A2,
  input  A4,
  output OUT1,
  output OUT3,
  output OUT2,
  output OUT4,
  output CARRY
);

  wire and_1_out, and_2_out, and_3_out;

  xor xor_1 (OUT1, A1, B);
  and and_1 (and_1_out, B, A1);
  xor xor_2 (OUT2, A2, and_1_out);
  and and_2 (and_2_out, and_1_out, A2);
  xor xor_3 (OUT3, A3, and_2_out);
  and and_3 (and_3_out, and_2_out, A3);
  xor xor_4 (OUT4, A4, and_3_out);
  and and_4 (CARRY, and_3_out, A4);
endmodule
