// Logisim project IICSE_076_ASS02_03.circ as structural Verilog: 1 circuit, main circuit main
module main (
  input  A1,
  input  A3,
  input  B,
  input  A2,
  input  A4,
  output O1,
  output O3,
  output O2,
  output O4,
  output B_OUT
);

  wire and_1_out, and_2_out, and_3_out, not_1_out, not_2_out, not_3_out, not_4_out;

  not not_1 (not_1_out, A1);
  not not_2 (not_2_out, A2);
  xor xor_1 (O1, A1, B);
  and and_1 (and_1_out, B, not_1_out);
  xor xor_2 (O2, A2, and_1_out);
  and and_2 (and_2_out, and_1_out, not_2_out);
  xor xor_3 (O3, A3, and_2_out);
  not not_3 (not_3_out, A3);
  not not_4 (not_4_out, A4);
  and and_3 (and_3_out, and_2_out, not_3_out);
  xor xor_4 (O4, A4, and_3_out);
  and and_4 (B_OUT, and_3_out, not_4_out);

  // Notes on the sheet:
  //   OUT 1
  //   OUT 2
endmodule
