// Logisim project IICSE_076_ASS02_04.circ as structural Verilog: 1 circuit, main circuit main
module main (
  input  A1,
  input  A3,
  input  B1,
  input  B3,
  input  C,
  input  A2,
  input  A4,
  input  B2,
  input  in_9,
  output O1,
  output o3,
  output O2,
  output O4,
  output C_OUT
);

  wire and_1_out, and_2_out, and_3_out, and_4_out, and_5_out, and_6_out, and_7_out, and_8_out, not_1_out,
       not_2_out, not_3_out, not_4_out, not_5_out, not_6_out, not_7_out, not_8_out, or_1_out, or_2_out,
       or_3_out, xor_1_out, xor_2_out, xor_5_out, xor_6_out;

  not not_1 (not_1_out, A1);
  not not_2 (not_2_out, A2);
  xor xor_1 (xor_1_out, A1, B1);
  and and_1 (and_1_out, B1, not_1_out);
  xor xor_2 (xor_2_out, A2, B2);
  and and_2 (and_2_out, B2, not_2_out);
  xor xor_3 (O1, xor_1_out, C);
  not not_3 (not_3_out, C);
  xor xor_4 (O2, xor_2_out, or_1_out);
  not not_4 (not_4_out, or_1_out);
  and and_3 (and_3_out, not_4_out, xor_2_out);
  and and_4 (and_4_out, not_3_out, xor_1_out);
  or or_1 (or_1_out, and_4_out, and_1_out);
  or or_2 (or_2_out, and_3_out, and_2_out);
  not not_5 (not_5_out, A3);
  not not_6 (not_6_out, A4);
  xor xor_5 (xor_5_out, A3, B3);
  and and_5 (and_5_out, B3, not_5_out);
  xor xor_6 (xor_6_out, A4, in_9);
  and and_6 (and_6_out, in_9, not_6_out);
  not not_7 (not_7_out, or_2_out);
  xor xor_7 (o3, xor_5_out, or_2_out);
  and and_7 (and_7_out, not_7_out, xor_5_out);
  xor xor_8 (O4, xor_6_out, or_3_out);
  and and_8 (and_8_out, not_8_out, xor_6_out);
  not not_8 (not_8_out, or_3_out);
  or or_3 (or_3_out, and_7_out, and_5_out);
  or or_4 (C_OUT, and_8_out, and_6_out);
endmodule
