// Logisim project IICSE_076_ASS02_05.circ as structural Verilog: 1 circuit, main circuit main
module main (
  input  A1,
  input  A4,
  input  A7,
  input  B,
  input  A2,
  input  A5,
  input  A8,
  input  A6,
  input  A3,
  output O1,
  output O4,
  output O7,
  output O2,
  output O5,
  output O8,
  output carry_out,
  output O6,
  output O3
);

  wire and_1_out, and_2_out, and_3_out, and_4_out, and_5_out, and_6_out, and_7_out;

  xor xor_1 (O1, A1, B);
  and and_1 (and_1_out, B, A1);
  xor xor_2 (O2, A2, and_1_out);
  and and_2 (and_2_out, and_1_out, A2);
  xor xor_3 (O3, A3, and_2_out);
  and and_3 (and_3_out, and_2_out, A3);
  xor xor_4 (O4, A4, and_3_out);
  and and_4 (and_4_out, and_3_out, A4);
  xor xor_5 (O5, A5, and_4_out);
  and and_5 (and_5_out, and_4_out, A5);
  xor xor_6 (O6, A6, and_5_out);
  and and_6 (and_6_out, and_5_out, A6);
  xor xor_7 (O7, A7, and_6_out);
  and and_7 (and_7_out, and_6_out, A7);
  xor xor_8 (O8, A8, and_7_out);
  and and_8 (carry_out, and_7_out, A8);
endmodule
